// Logisim project ALU.circ as structural Verilog: 3 circuits, main circuit main
module main (
  input  OPCODE_0,
  input  OPCODE_1,
  input  OPCODE_2,
  input  ALT_OPCODE,
  input  INPUT0_0,
  input  INPUT0_1,
  input  INPUT0_2,
  input  INPUT0_3,
  input  INPUT1_0,
  input  INPUT1_1,
  input  INPUT1_2,
  input  INPUT1_3,
  output OUTPUT0_0,
  output OUTPUT0_1,
  output OUTPUT0_2,
  output OUTPUT0_3,
  output OUTPUT1_0,
  output OUTPUT1_1,
  output OUTPUT1_2,
  output OUTPUT1_3,
  output CARRY,
  output NEGATIVE,
  output OVERFLOW,
  output ZERO
);
endmodule

module half_adder (
  input  INPUT_0,
  input  INPUT_1,
  output RESULT,
  output CARRY
);

  xor xor_1 (RESULT, INPUT_0, INPUT_1);
  and and_1 (CARRY, INPUT_0, INPUT_1);
endmodule

module full_adder_1_bit (
  input  INPUT_0,
  input  INPUT_1,
  input  CARRY_IN,
  output SUM,
  output CARRY_OUT
);

  wire half_adder_1_carry, half_adder_1_result, half_adder_2_carry;

  half_adder half_adder_1 (
    .INPUT_0(INPUT_0), .INPUT_1(INPUT_1), .RESULT(half_adder_1_result), .CARRY(half_adder_1_carry));
  half_adder half_adder_2 (.INPUT_0(half_adder_1_result), .INPUT_1(CARRY_IN), .RESULT(SUM), .CARRY(half_adder_2_carry));
  or or_1 (CARRY_OUT, half_adder_2_carry, half_adder_1_carry);
endmodule
